# Fritzing sketch pad (saved by Fritzing 0.9.3b)

parts:
  Part1 = Arduino Micro (Rev3)
  U1 = SLIDER [package=slider]
  U2 = SLIDER [package=slider]
  U3 = SLIDER [package=slider]
  Generic_4x4_button_keypad1 = Generic 4x4 Keypad
  S1 = Taiway 100-SP-X-T1 SPDT Miniature Toggle Switch [part_number=100-SP-X-T1-0-0-B1-M2 package=THT]
  S2 = Taiway 100-SP-X-T1 SPDT Miniature Toggle Switch [part_number=100-SP-X-T1-0-0-B1-M2 package=THT]
  S3 = Taiway 100-SP-X-T1 SPDT Miniature Toggle Switch [part_number=100-SP-X-T1-0-0-B1-M2 package=THT]
  SW1 = ENCODER_RGB_CA [package=encoder_led_3]
  SW2 = ENCODER_RGB_CA [package=encoder_led_3]
  SW3 = ENCODER_RGB_CA [package=encoder_led_3]
  SW4 = ENCODER_RGB_CA [package=encoder_led_3]
  MCP23S1 = MCP23S17 I2C I/O Expander

nets:
  N1: Part1.MOSI, MCP23S1.SI
  N2: Part1.RXLED/SS, MCP23S1.CS
  GND: Part1.GND, U1.E, U2.E, U3.E, S1.COM, S2.COM, S3.COM, SW4.C, MCP23S1.VSS, MCP23S1.A0
  N3: Part1.D2/SDA, S3.L2
  N4: Part1.D3/SCL, S2.L2
  N5: Part1.D4_PWM/A6, S1.L2
  N6: Part1.D5_PWM, Generic_4x4_button_keypad1.R4
  N7: Part1.D6_PWM/A7, Generic_4x4_button_keypad1.R3
  N8: Part1.D7, Generic_4x4_button_keypad1.R2
  N9: Part1.D8_PWM/A8, Generic_4x4_button_keypad1.R1
  N10: Part1.D9_PWM/A9, Generic_4x4_button_keypad1.C1
  N11: Part1.D10_PWM/A10, Generic_4x4_button_keypad1.C2
  N12: Part1.D11_PWM, Generic_4x4_button_keypad1.C3
  N13: Part1.D12_PWM/A11, Generic_4x4_button_keypad1.C4
  N14: Part1.SCK, MCP23S1.SCK
  N15: Part1.MISO, MCP23S1.SO
  5V: Part1.5V, U1.A, U2.A, U3.A, MCP23S1.VDD, MCP23S1.RESET
  N16: Part1.A2, U3.S
  N17: Part1.A1, U2.S
  N18: Part1.A0, U1.S
  N19: SW1.-B, MCP23S1.GPA6
  N20: SW1.+, MCP23S1.GPB1
  N21: SW1.A, MCP23S1.GPB0
  N22: SW2.-B, MCP23S1.GPA4
  N23: SW2.+, MCP23S1.GPA5
  N24: SW2.A, MCP23S1.GPB2
  N25: SW3.-B, MCP23S1.GPB5
  N26: SW3.+, MCP23S1.GPB4
  N27: SW3.A, MCP23S1.GPB3
  N28: SW4.-B, MCP23S1.GPA7
  N29: SW4.+, MCP23S1.GPB7
  N30: SW4.A, MCP23S1.GPB6

custom parts:
  Generic 4x4 Keypad: generic 4x4 keypad 4 rows of four 6 mm tact switches cheap and nasty but works
  MCP23S17 I2C I/O Expander: The MCP23017 uses two i2c pins (these can be shared with other i2c devices), and in exchange gives you 16 general purpose pins. You can set each of 16 pins to be input, output, input with a pullup or open drain. There's even the ability to get an interrupt via an external pin when any of the inputs change so you don't have to keep polling the chip.
